# Fritzing sketch diagrama (saved by Fritzing 0.9.2b)
breadboards: 1

parts:
  KY-1 = Keyes Relay [package=THT]
  Parte1 = Arduino Uno (Rev3)
  VCC1 = Battery block 9V
  M1 = DC Motor

nets:
  N1: KY-1.signal, Parte1.D8
  N2: KY-1.power, Parte1.5V
  N3: KY-1.ground, Parte1.GND
  N4: KY-1.C, VCC1.+
  N5: KY-1.NO, M1.pin_1
  N6: VCC1.-, M1.pin_2

custom parts:
  Keyes Relay: The Keyes 5V relay module is suitable for SCM development, home appliance control. It uses a 5V~12V TIL control signal which can control DC / AC signal.
