# Fritzing sketch ejercicio30 (saved by Fritzing 0.9.2b)
breadboards: 1

parts:
  Parte1 = Arduino Uno (Rev3)
  LED1 = LED - 5mm [color="Red (633nm)" package="5 mm [THT]"]
  LED2 = LED - 5mm [color="Yellow (592nm)" package="5 mm [THT]"]
  LED3 = LED - 5mm [color="Green (555nm)" package="5 mm [THT]"]
  LED4 = LED - 5mm [color="Blue (525nm)" package="5 mm [THT]"]
  R1 = Resistor [tolerance=±5% resistance=220 package=THT]
  R2 = Resistor [tolerance=±5% resistance=220 package=THT]
  R3 = Resistor [tolerance=±5% resistance=220 package=THT]
  R4 = Resistor [tolerance=±5% resistance=220 package=THT]

nets:
  N1: Parte1.D8, LED1.anode
  N2: Parte1.D9_PWM, LED2.anode
  N3: Parte1.D10_PWM/SS, LED3.anode
  N4: Parte1.D11_PWM/MOSI, LED4.anode
  N5: Parte1.GND, R1.Pin_1, R2.Pin_1, R3.Pin_1, R4.Pin_1
  N6: LED1.cathode, R1.Pin_0
  N7: LED2.cathode, R2.Pin_0
  N8: LED3.cathode, R3.Pin_0
  N9: LED4.cathode, R4.Pin_0
