# Fritzing sketch ejercicio11 (saved by Fritzing 0.9.2b)
breadboards: 1

parts:
  Parte1 = Arduino Uno (Rev3)
  LED1 = LED - 5mm [color="Red (633nm)" package="5 mm [THT]"]
  R1 = Resistor [tolerance=±5% resistance=220 package=THT]
  R2 = Photocell (LDR) [package=THT]
  R3 = Resistor [tolerance=±5% resistance=1.5k package=THT]
  J1 = Basic Servo

nets:
  N1: Parte1.A0, R2.pin_1, R3.Pin_0
  N2: Parte1.D8, J1.pulse
  N3: Parte1.D7, LED1.anode
  5V: Parte1.5V, R2.pin_0, J1.vcc
  GND: Parte1.GND, R1.Pin_1, R3.Pin_1, J1.gnd
  N4: LED1.cathode, R1.Pin_0
