# Fritzing sketch diagrama (saved by Fritzing 0.9.2b)
breadboards: 1

parts:
  Parte1 = Arduino Uno (Rev3)
  Q1 = NPN-Transistor [package="TO92 [THT]"]
  M1 = DC Motor
  R1 = Resistor [tolerance=±5% resistance=1k package=THT]

nets:
  N1: Parte1.D8, R1.Pin_0
  N2: Parte1.5V, M1.pin_2
  N3: Parte1.GND, Q1.E
  N4: Q1.B, R1.Pin_1
  N5: Q1.C, M1.pin_1
