# Fritzing sketch diagrama (saved by Fritzing 0.9.2b)
breadboards: 1

parts:
  Parte1 = Arduino Uno (Rev3)
  IC1 = H-Bridge [package=THT]
  R1 = Rotary Potentiometer (Small) [maximum_resistance=100kΩ package=THT]
  VCC1 = Battery block 9V
  M1 = DC Motor  # not connected

nets:
  N1: Parte1.A0, R1.wiper
  N2: Parte1.5V, IC1.VCC1, R1.leg2
  GND: Parte1.GND, IC1.GND3, IC1.GND4, R1.leg1, VCC1.-
